# Fritzing sketch RPiBrushlessMotor (saved by Fritzing 0.9.3b)

parts:
  M1 = ESC
  Power_plug1 = Power plug  # not connected
  920KV_Motor1 = DJI 920 KV Motor
  Raspberry_Pi_1 = Raspberry Pi 3 [part_number=RPI-3-V1.2]
  U1 = LIPO-1000mAh [package=lipo-1000]  # not connected

nets:
  N1: M1.U, 920KV_Motor1.u
  N2: M1.V, 920KV_Motor1.v
  N3: M1.W, 920KV_Motor1.w
  N4: M1.DATA, Raspberry_Pi_1.GPIO18
  GND: M1.GND, Raspberry_Pi_1.GND

notes:
  5V 2A
  Lipo battery 3s 11.1v

custom parts:
  DJI 920 KV Motor: DJI Brushless Outrunner 2212/920K Motor F330-550
