# Fritzing sketch RPiI2C (saved by Fritzing 0.9.3b)

parts:
  Raspberry_Pi_1 = Raspberry Pi 3 [part_number=RPI-3-V1.2]
  GY1 = MPU-6050 Board GY-521 [form="♀ (female)" package=THT]

nets:
  N1: Raspberry_Pi_1.3v3, GY1.pin1
  N2: Raspberry_Pi_1.GPIO2, GY1.pin4
  N3: Raspberry_Pi_1.GPIO3, GY1.pin3
  N4: Raspberry_Pi_1.GND, GY1.pin2

custom parts:
  MPU-6050 Board GY-521: Acelerometro y Giroscopio MPU-6050 Board GY-521
