# Fritzing sketch RPiStepMotor (saved by Fritzing 0.9.3b)

parts:
  Raspberry_Pi_1 = Raspberry Pi 3 [part_number=RPI-3-V1.2]
  Power_plug1 = Power plug  # not connected
  Part1 = EasyDriver_v44
  U1 = LIPO-1000mAh [package=lipo-1000]
  M2 = Stepper Motor - Bipolar

nets:
  N1: Raspberry_Pi_1.GPIO17, Part1.DIR
  N2: Raspberry_Pi_1.GPIO27, Part1.SLEEP
  GND: Raspberry_Pi_1.GND, Part1.GND, U1.-
  N3: Raspberry_Pi_1.GPIO18, Part1.STEP
  N4: Part1.V+, U1.+
  N5: Part1.OUT2A, M2.A
  N6: Part1.OUT2B, M2.C
  N7: Part1.OUT1A, M2.B
  N8: Part1.OUT1B, M2.D
