# Fritzing sketch watersensor (saved by Fritzing 0.9.3b)

parts:
  Raspberry_Pi_1 = Raspberry Pi 3 [part_number=RPI-3-V1.2]
  R1 = Resistor [tolerance=±5% resistance=220 package=THT]

nets:
  N1: Raspberry_Pi_1.GND, R1.Pin_0
  N2: Raspberry_Pi_1.GPIO14, R1.Pin_1
